// Logisim project cpu.circ as structural Verilog: 10 circuits, main circuit main
module main (
  input  reset
);

  wire alu_sec_output, ALUinB, and_8_out, BR, clk, decoder_1_out0, decoder_1_out1, decoder_1_out2,
       decoder_1_out7, decoder_1_out8, decoder_1_out9, decoder_1_out11, decoder_1_out12, decoder_1_out13,
       display_output, DMwe, jal, jump, jump_return, keyboard_is, keyboard_valid, memory_latch_1_oe_latched,
       memory_latch_1_we_latched, nclk, not_3_out, optype_add, optype_biggerOrEqual, optype_leftShift,
       optype_nand, optype_nor, optype_rightShift, optype_sub, or_12_out, Rdst, Rwd, Rwe;
  wire [2:0] multiplexer_1_out, multiplexer_2_out, optype, Rd, Rs, Rt, shamt;
  wire [3:0] opcode;
  wire [5:0] Imm;
  wire [6:0] keyboard_1_data;
  wire [7:0] keyboard_output;
  wire [15:0] address, alu_2_aluoutput, alu_3_aluoutput, controlled_buffer_8_out, ImmSX, instruction_code,
       memory_latch_1_address_latched, memory_latch_1_data_in_latched, multiplexer_3_out, multiplexer_4_out,
       multiplexer_5_out, multiplexer_6_out, multiplexer_7_out, multiplexer_8_out, multiplexer_9_out,
       PC_output_16_bit, PCplus1, R1Data, R2Data, ram_1_dout;

  Decoder #(.select(4)) decoder_1 (
    .out0(decoder_1_out0), .out1(decoder_1_out1), .out2(decoder_1_out2), .out3(optype_nor),
    .out4(optype_nand), .out5(optype_leftShift), .out6(optype_rightShift), .out7(decoder_1_out7),
    .out8(decoder_1_out8), .out9(decoder_1_out9), .out10(optype_biggerOrEqual), .out11(decoder_1_out11),
    .out12(decoder_1_out12), .out13(decoder_1_out13), .out14(keyboard_is), .out15(display_output),
    .sel(opcode));  // open: en
  or or_1 (BR, decoder_1_out9, optype_biggerOrEqual);
  assign optype = optype_add ? 3'b000 : 3'bz;  // Controlled_Buffer controlled_buffer_1
  assign optype = optype_nor ? 3'b010 : 3'bz;  // Controlled_Buffer controlled_buffer_2
  assign optype = optype_nand ? 3'b011 : 3'bz;  // Controlled_Buffer controlled_buffer_3
  assign optype = optype_sub ? 3'b001 : 3'bz;  // Controlled_Buffer controlled_buffer_4
  assign optype = optype_leftShift ? 3'b100 : 3'bz;  // Controlled_Buffer controlled_buffer_5
  assign optype = optype_rightShift ? 3'b101 : 3'bz;  // Controlled_Buffer controlled_buffer_6
  assign optype = optype_biggerOrEqual ? 3'b110 : 3'bz;  // Controlled_Buffer controlled_buffer_7
  Clock clock_1 (.out(clk));
  buf or_2 (jal, decoder_1_out13);  // OR_Gate
  not not_1 (nclk, clk);
  buf or_3 (jump, decoder_1_out11);  // OR_Gate
  buf or_4 (jump_return, decoder_1_out12);  // OR_Gate
  OneReg PC (.reset(reset), .clk(nclk), .WEn(1'b1), .input_16_bit(multiplexer_8_out), .output_16_bit(PC_output_16_bit));
  // Probe on PC_output_16_bit
  ROM #(.addrWidth(16), .dataWidth(16)) rom_1 (.addr(PC_output_16_bit), .data(instruction_code));
  or or_5 (Rdst, optype_rightShift, optype_leftShift, optype_nor, decoder_1_out2, optype_nand, decoder_1_out0);
  Keyboard keyboard_1 (.clk(nclk), .re(keyboard_is), .clr(reset), .avail(keyboard_valid), .data(keyboard_1_data));
  instruction_decoder instruction_decoder_1 (
    .instruction_code(instruction_code), .Rt(Rt), .address(address), .Rs(Rs), .opcode(opcode), .Rd(Rd),
    .Imm(Imm), .shamt(shamt));
  or or_6 (ALUinB, decoder_1_out8, decoder_1_out7, decoder_1_out1, optype_leftShift, optype_rightShift);
  assign controlled_buffer_8_out = display_output ? R1Data : 16'bz;  // Controlled_Buffer controlled_buffer_8
  alu alu_1 (.A(16'h1), .B(PC_output_16_bit), .OpType(3'b000), .aluOutput(PCplus1));  // open: sec_output
  or or_7 (Rwe, keyboard_is, decoder_1_out13, decoder_1_out7, optype_rightShift, optype_leftShift, decoder_1_out0, optype_nand, optype_nor, decoder_1_out1, decoder_1_out2);
  // Probe on instruction_code
  buf or_8 (DMwe, decoder_1_out8);  // OR_Gate
  not not_2 (keyboard_output[7], keyboard_valid);
  buf or_9 (Rwd, decoder_1_out7);  // OR_Gate
  and and_1 (keyboard_output[0], keyboard_valid, keyboard_1_data[0]);
  and and_2 (keyboard_output[1], keyboard_1_data[1], keyboard_valid);
  and and_3 (keyboard_output[2], keyboard_1_data[2], keyboard_valid);
  and and_4 (keyboard_output[3], keyboard_1_data[3], keyboard_valid);
  Multiplexer #(.width(3), .enable("false")) multiplexer_1 (.in0(Rt), .in1(Rd), .out(multiplexer_1_out), .sel(Rdst));
  or or_10 (optype_add, decoder_1_out1, decoder_1_out0, decoder_1_out7, decoder_1_out8);
  and and_5 (keyboard_output[4], keyboard_1_data[4], keyboard_valid);
  and and_6 (keyboard_output[5], keyboard_1_data[5], keyboard_valid);
  and and_7 (keyboard_output[6], keyboard_1_data[6], keyboard_valid);
  TTY #(.rows(13), .cols(80)) tty_1 (.data(controlled_buffer_8_out[6:0]), .clk(clk), .we(display_output), .clr(reset));
  Multiplexer #(.width(3), .enable("false")) multiplexer_2 (
    .in0(multiplexer_1_out), .in1(3'b111), .out(multiplexer_2_out), .sel(jal));
  // Probe on Imm
  Multiplexer #(.width(16), .enable("false")) multiplexer_3 (
    .in0(multiplexer_9_out), .in1(PCplus1), .out(multiplexer_3_out), .sel(jal));
  alu alu_2 (.A(PCplus1), .B(ImmSX), .OpType(3'b000), .aluOutput(alu_2_aluoutput));  // open: sec_output
  Multiplexer #(.width(16), .enable("false")) multiplexer_4 (
    .in0(multiplexer_3_out), .in1({{8{1'b0}}, keyboard_output}), .out(multiplexer_4_out), .sel(keyboard_is));
  signExtension signextension_1 (.input_val(Imm), .result(ImmSX));
  not not_3 (not_3_out, alu_sec_output);
  RegisterFile registerfile_1 (
    .reset(reset), .RegWSel(multiplexer_2_out), .clk(clk), .RegR1Sel(Rs), .RegWE(Rwe), .RegR2Sel(Rt),
    .DataIn(multiplexer_4_out), .R1Data(R1Data), .R2Data(R2Data));
  or or_11 (optype_sub, decoder_1_out2, decoder_1_out9);
  Multiplexer #(.width(16), .enable("false")) multiplexer_5 (
    .in0(PCplus1), .in1(alu_2_aluoutput), .out(multiplexer_5_out), .sel(and_8_out));
  and and_8 (and_8_out, BR, not_3_out);
  Multiplexer #(.width(16), .enable("false")) multiplexer_6 (
    .in0(multiplexer_5_out), .in1(address), .out(multiplexer_6_out), .sel(or_12_out));
  or or_12 (or_12_out, jump, jal);
  // Probe on ImmSX
  // Probe on R1Data
  Multiplexer #(.width(16), .enable("false")) multiplexer_7 (
    .in0(R2Data), .in1(ImmSX), .out(multiplexer_7_out), .sel(ALUinB));
  Multiplexer #(.width(16), .enable("false")) multiplexer_8 (
    .in0(multiplexer_6_out), .in1(R1Data), .out(multiplexer_8_out), .sel(jump_return));
  // Probe on multiplexer_7_out
  // Probe on multiplexer_9_out
  // Probe on optype
  alu alu_3 (
    .A(R1Data), .B(multiplexer_7_out), .OpType(optype), .aluOutput(alu_3_aluoutput),
    .sec_output(alu_sec_output));
  memory_latch memory_latch_1 (
    .address(alu_3_aluoutput), .WE(DMwe), .clk(nclk), .data_in(R2Data),
    .address_latched(memory_latch_1_address_latched), .WE_latched(memory_latch_1_we_latched),
    .OE_latched(memory_latch_1_oe_latched), .data_in_latched(memory_latch_1_data_in_latched));
  RAM #(.addrWidth(16), .dataWidth(16), .trigger("high"), .databus("bibus")) ram_1 (
    .addr(memory_latch_1_address_latched), .we(memory_latch_1_we_latched), .oe(memory_latch_1_oe_latched),
    .din(memory_latch_1_data_in_latched), .dout(ram_1_dout));
  Multiplexer #(.width(16), .enable("false")) multiplexer_9 (
    .in0(alu_3_aluoutput), .in1(ram_1_dout), .out(multiplexer_9_out), .sel(Rwd));

  // Notes on the sheet:
  //   add
  //   contents of rom_1 (hex, n*v repeats v):
  //   104a e040 12a0 f400 e040 12a0 f400 e040 12a0 f400 903f
  //   addi
  //   nor
  //   sub
  //   nand
  //   sll
  //   srl
  //   lw
  //   sw
  //   beq
  //   bge
  //   jump
  //   jr
  //   jal
  //   input
  //   output
endmodule

module memory_latch (
  input  [15:0] address,
  input  WE,
  input  clk,
  input  [15:0] data_in,
  output [15:0] address_latched,
  output WE_latched,
  output OE_latched,
  output [15:0] data_in_latched
);

  wire DMwe_latch_q;
  wire [15:0] addr_latch_q;

  Register #(.width(16), .trigger("falling")) addr_latch (
    .D(address), .en(WE), .clk(clk), .Q(addr_latch_q));  // open: clr
  D_Flip_Flop #(.trigger("falling")) DMwe_latch (.D(WE), .clk(clk), .Q(DMwe_latch_q));  // open: Qn, preset, reset
  Register #(.width(16), .trigger("falling")) data_to_be_written (
    .D(data_in), .en(WE), .clk(clk), .Q(data_in_latched));  // open: clr
  Multiplexer #(.width(16), .enable("false")) multiplexer_1 (
    .in0(address), .in1(addr_latch_q), .out(address_latched), .sel(DMwe_latch_q));
  and and_1 (WE_latched, clk, DMwe_latch_q);
  not not_1 (OE_latched, WE_latched);
endmodule

module OneReg (
  input  reset,
  input  clk,
  input  WEn,
  input  [15:0] input_16_bit,
  output [15:0] output_16_bit
);

  wire clk_enable;

  D_Flip_Flop d_ff_1 (
    .D(input_16_bit[15]), .clk(clk_enable), .Q(output_16_bit[15]), .reset(reset));  // open: Qn, preset
  D_Flip_Flop d_ff_2 (.D(input_16_bit[7]), .clk(clk_enable), .Q(output_16_bit[7]), .reset(reset));  // open: Qn, preset
  D_Flip_Flop d_ff_3 (
    .D(input_16_bit[14]), .clk(clk_enable), .Q(output_16_bit[14]), .reset(reset));  // open: Qn, preset
  D_Flip_Flop d_ff_4 (.D(input_16_bit[6]), .clk(clk_enable), .Q(output_16_bit[6]), .reset(reset));  // open: Qn, preset
  and and_1 (clk_enable, clk, WEn);
  D_Flip_Flop d_ff_5 (
    .D(input_16_bit[13]), .clk(clk_enable), .Q(output_16_bit[13]), .reset(reset));  // open: Qn, preset
  D_Flip_Flop d_ff_6 (.D(input_16_bit[5]), .clk(clk_enable), .Q(output_16_bit[5]), .reset(reset));  // open: Qn, preset
  D_Flip_Flop d_ff_7 (
    .D(input_16_bit[12]), .clk(clk_enable), .Q(output_16_bit[12]), .reset(reset));  // open: Qn, preset
  D_Flip_Flop d_ff_8 (.D(input_16_bit[4]), .clk(clk_enable), .Q(output_16_bit[4]), .reset(reset));  // open: Qn, preset
  D_Flip_Flop d_ff_9 (
    .D(input_16_bit[11]), .clk(clk_enable), .Q(output_16_bit[11]), .reset(reset));  // open: Qn, preset
  D_Flip_Flop d_ff_10 (.D(input_16_bit[3]), .clk(clk_enable), .Q(output_16_bit[3]), .reset(reset));  // open: Qn, preset
  D_Flip_Flop d_ff_11 (
    .D(input_16_bit[10]), .clk(clk_enable), .Q(output_16_bit[10]), .reset(reset));  // open: Qn, preset
  D_Flip_Flop d_ff_12 (.D(input_16_bit[2]), .clk(clk_enable), .Q(output_16_bit[2]), .reset(reset));  // open: Qn, preset
  D_Flip_Flop d_ff_13 (.D(input_16_bit[9]), .clk(clk_enable), .Q(output_16_bit[9]), .reset(reset));  // open: Qn, preset
  D_Flip_Flop d_ff_14 (.D(input_16_bit[1]), .clk(clk_enable), .Q(output_16_bit[1]), .reset(reset));  // open: Qn, preset
  D_Flip_Flop d_ff_15 (.D(input_16_bit[8]), .clk(clk_enable), .Q(output_16_bit[8]), .reset(reset));  // open: Qn, preset
  D_Flip_Flop d_ff_16 (.D(input_16_bit[0]), .clk(clk_enable), .Q(output_16_bit[0]), .reset(reset));  // open: Qn, preset

  // Other names for the same wires on the sheet: enable = WEn; In0 = input_16_bit[0]; In1 = input_16_bit[1];
  //   In2 = input_16_bit[2]; In3 = input_16_bit[3]; In4 = input_16_bit[4]; In5 = input_16_bit[5];
  //   In6 = input_16_bit[6]; In7 = input_16_bit[7]; In8 = input_16_bit[8]; In9 = input_16_bit[9];
  //   In10 = input_16_bit[10]; In11 = input_16_bit[11]; In12 = input_16_bit[12]; In13 = input_16_bit[13];
  //   In14 = input_16_bit[14]; In15 = input_16_bit[15]; R0 = output_16_bit[0]; R1 = output_16_bit[1];
  //   R2 = output_16_bit[2]; R3 = output_16_bit[3]; R4 = output_16_bit[4]; R5 = output_16_bit[5];
  //   R6 = output_16_bit[6]; R7 = output_16_bit[7]; R8 = output_16_bit[8]; R9 = output_16_bit[9];
  //   R10 = output_16_bit[10]; R11 = output_16_bit[11]; R12 = output_16_bit[12]; R13 = output_16_bit[13];
  //   R14 = output_16_bit[14]; R15 = output_16_bit[15]
endmodule

module RegisterFile (
  input  reset,
  input  [2:0] RegWSel,
  input  clk,
  input  [2:0] RegR1Sel,
  input  RegWE,
  input  [2:0] RegR2Sel,
  input  [15:0] DataIn,
  output [15:0] R1Data,
  output [15:0] R2Data
);

  wire R1_0, R1_1, R1_2, R1_3, R1_4, R1_5, R1_6, R1_7, R2_0, R2_1, R2_2, R2_3, R2_4, R2_5, R2_6, R2_7, WE0,
       WE1, WE2, WE3, WE4, WE5, WE6, WE7;
  wire [15:0] Q0, Q1, Q2, Q3, Q4, Q5, Q6, Q7;

  assign R1Data = R1_7 ? Q7 : 16'bz;  // Controlled_Buffer controlled_buffer_1
  assign R1Data = R1_6 ? Q6 : 16'bz;  // Controlled_Buffer controlled_buffer_2
  assign R1Data = R1_5 ? Q5 : 16'bz;  // Controlled_Buffer controlled_buffer_3
  assign R1Data = R1_4 ? Q4 : 16'bz;  // Controlled_Buffer controlled_buffer_4
  assign R1Data = R1_3 ? Q3 : 16'bz;  // Controlled_Buffer controlled_buffer_5
  assign R1Data = R1_2 ? Q2 : 16'bz;  // Controlled_Buffer controlled_buffer_6
  assign R1Data = R1_1 ? Q1 : 16'bz;  // Controlled_Buffer controlled_buffer_7
  assign R1Data = R1_0 ? Q0 : 16'bz;  // Controlled_Buffer controlled_buffer_8
  OneReg reg7 (.reset(reset), .clk(clk), .WEn(WE7), .input_16_bit(DataIn), .output_16_bit(Q7));
  OneReg reg3 (.reset(reset), .clk(clk), .WEn(WE3), .input_16_bit(DataIn), .output_16_bit(Q3));
  // Probe on Q3
  // Probe on Q7
  assign R2Data = R2_7 ? Q7 : 16'bz;  // Controlled_Buffer controlled_buffer_9
  assign R2Data = R2_6 ? Q6 : 16'bz;  // Controlled_Buffer controlled_buffer_10
  assign R2Data = R2_5 ? Q5 : 16'bz;  // Controlled_Buffer controlled_buffer_11
  assign R2Data = R2_4 ? Q4 : 16'bz;  // Controlled_Buffer controlled_buffer_12
  assign R2Data = R2_3 ? Q3 : 16'bz;  // Controlled_Buffer controlled_buffer_13
  assign R2Data = R2_2 ? Q2 : 16'bz;  // Controlled_Buffer controlled_buffer_14
  assign R2Data = R2_1 ? Q1 : 16'bz;  // Controlled_Buffer controlled_buffer_15
  assign R2Data = R2_0 ? Q0 : 16'bz;  // Controlled_Buffer controlled_buffer_16
  OneReg reg6 (.reset(reset), .clk(clk), .WEn(WE6), .input_16_bit(DataIn), .output_16_bit(Q6));
  OneReg reg2 (.reset(reset), .clk(clk), .WEn(WE2), .input_16_bit(DataIn), .output_16_bit(Q2));
  // Probe on Q2
  // Probe on Q6
  Decoder #(.select(3)) decoder_1 (
    .out0(WE0), .out1(WE1), .out2(WE2), .out3(WE3), .out4(WE4), .out5(WE5), .out6(WE6), .out7(WE7),
    .sel(RegWSel), .en(RegWE));
  Decoder #(.select(3)) decoder_2 (
    .out0(R1_0), .out1(R1_1), .out2(R1_2), .out3(R1_3), .out4(R1_4), .out5(R1_5), .out6(R1_6), .out7(R1_7),
    .sel(RegR1Sel));  // open: en
  OneReg reg5 (.reset(reset), .clk(clk), .WEn(WE5), .input_16_bit(DataIn), .output_16_bit(Q5));
  // Probe on Q5
  OneReg reg1 (.reset(reset), .clk(clk), .WEn(WE1), .input_16_bit(DataIn), .output_16_bit(Q1));
  // Probe on Q1
  Decoder #(.select(3)) decoder_3 (
    .out0(R2_0), .out1(R2_1), .out2(R2_2), .out3(R2_3), .out4(R2_4), .out5(R2_5), .out6(R2_6), .out7(R2_7),
    .sel(RegR2Sel));  // open: en
  OneReg reg0 (.reset(reset), .clk(clk), .WEn(1'b0), .input_16_bit({16{1'b0}}), .output_16_bit(Q0));
  OneReg reg4 (.reset(reset), .clk(clk), .WEn(WE4), .input_16_bit(DataIn), .output_16_bit(Q4));
  // Probe on Q0
  // Probe on Q4

  // Other names for the same wires on the sheet: Data[15:0] = DataIn
endmodule

module alu (
  input  [15:0] A,
  input  [15:0] B,
  input  [2:0] OpType,
  output [15:0] aluOutput,
  output sec_output
);

  wire BE, equal;
  wire [14:0] sub;
  wire [15:0] add, left_shift, nand_nand, nor_nor, not_not, or_or, right_shift;

  assign nor_nor = ~(A | B);  // NOR_Gate nor_1, 16 bits wide
  assign nand_nand = ~(A & B);  // NAND_Gate nand_1, 16 bits wide
  add_circuit add_circuit_1 (.B(B), .A(A), .sub(1'b0), .result(add));
  add_circuit add_circuit_2 (.B(B), .A(A), .sub(1'b1), .result({BE, sub}));
  assign or_or = A | B;  // OR_Gate or_1, 16 bits wide
  assign not_not = ~A;  // NOT_Gate not_1, 16 bits wide
  shifter_circuit shifter_circuit_1 (
    .A({A[0], A[1], A[2], A[3], A[4], A[5], A[6], A[7], A[8], A[9], A[10], A[11], A[12], A[13], A[14], A[15]}),
    .shift_bit(B[2:0]),
    .result({right_shift[0], right_shift[1], right_shift[2], right_shift[3], right_shift[4], right_shift[5], right_shift[6], right_shift[7], right_shift[8], right_shift[9], right_shift[10], right_shift[11], right_shift[12], right_shift[13], right_shift[14], right_shift[15]}));
  shifter_circuit shifter_circuit_2 (.A(A), .shift_bit(B[2:0]), .result(left_shift));
  Multiplexer #(.select(3), .width(16), .enable("false")) multiplexer_1 (
    .in0(add), .in1({BE, sub}), .in2(nor_nor), .in3(nand_nand), .in4(left_shift), .in5(right_shift),
    .in6({BE, sub}), .out(aluOutput), .sel(OpType));  // open: in7
  or or_2 (equal, sub[0], sub[1], sub[2], sub[3], sub[4], sub[5], sub[6], sub[7], sub[8], sub[9], sub[10], sub[11], sub[12], sub[13], sub[14], BE);
  Multiplexer #(.select(3), .enable("false")) multiplexer_2 (
    .in1(equal), .in6(BE), .out(sec_output), .sel(OpType));  // open: in0, in2, in3, in4, in5, in7

  // Other names for the same wires on the sheet: output_output[15:0] = aluOutput; shift_num[2:0] = B[2:0];
  //   sub[15] = BE

  // Notes on the sheet:
  //   ALU I/O
  //   ALU math and logic
  //   biggerOrEqual
endmodule

module add_circuit (
  input  [15:0] B,
  input  [15:0] A,
  input  sub,
  output [15:0] result
);

  wire C14, C15, full_adder_3_cout, full_adder_4_cout, full_adder_5_cout, full_adder_6_cout,
       full_adder_7_cout, full_adder_8_cout, full_adder_9_cout, full_adder_10_cout, full_adder_11_cout,
       full_adder_12_cout, full_adder_13_cout, full_adder_14_cout, full_adder_15_cout, full_adder_16_cout,
       xor_1_out, xor_2_out, xor_3_out, xor_4_out, xor_5_out, xor_6_out, xor_7_out, xor_8_out, xor_9_out,
       xor_10_out, xor_11_out, xor_12_out, xor_13_out, xor_14_out, xor_15_out, xor_16_out;

  full_adder full_adder_1 (.Cin(C14), .a(A[15]), .b(xor_1_out), .Sum(result[15]), .Cout(C15));
  xor xor_1 (xor_1_out, sub, B[15]);
  full_adder full_adder_2 (.Cin(full_adder_3_cout), .a(A[14]), .b(xor_2_out), .Sum(result[14]), .Cout(C14));
  xor xor_2 (xor_2_out, sub, B[14]);
  full_adder full_adder_3 (
    .Cin(full_adder_4_cout), .a(A[13]), .b(xor_3_out), .Sum(result[13]), .Cout(full_adder_3_cout));
  xor xor_3 (xor_3_out, sub, B[13]);
  full_adder full_adder_4 (
    .Cin(full_adder_5_cout), .a(A[12]), .b(xor_4_out), .Sum(result[12]), .Cout(full_adder_4_cout));
  xor xor_4 (xor_4_out, sub, B[12]);
  full_adder full_adder_5 (
    .Cin(full_adder_6_cout), .a(A[11]), .b(xor_5_out), .Sum(result[11]), .Cout(full_adder_5_cout));
  xor xor_5 (xor_5_out, sub, B[11]);
  full_adder full_adder_6 (
    .Cin(full_adder_7_cout), .a(A[10]), .b(xor_6_out), .Sum(result[10]), .Cout(full_adder_6_cout));
  xor xor_6 (xor_6_out, sub, B[10]);
  full_adder full_adder_7 (.Cin(full_adder_8_cout), .a(A[9]), .b(xor_7_out), .Sum(result[9]), .Cout(full_adder_7_cout));
  xor xor_7 (xor_7_out, sub, B[9]);
  full_adder full_adder_8 (.Cin(full_adder_9_cout), .a(A[8]), .b(xor_8_out), .Sum(result[8]), .Cout(full_adder_8_cout));
  xor xor_8 (xor_8_out, sub, B[8]);
  full_adder full_adder_9 (
    .Cin(full_adder_10_cout), .a(A[7]), .b(xor_9_out), .Sum(result[7]), .Cout(full_adder_9_cout));
  xor xor_9 (xor_9_out, sub, B[7]);
  full_adder full_adder_10 (
    .Cin(full_adder_11_cout), .a(A[6]), .b(xor_10_out), .Sum(result[6]), .Cout(full_adder_10_cout));
  xor xor_10 (xor_10_out, sub, B[6]);
  full_adder full_adder_11 (
    .Cin(full_adder_12_cout), .a(A[5]), .b(xor_11_out), .Sum(result[5]), .Cout(full_adder_11_cout));
  xor xor_11 (xor_11_out, sub, B[5]);
  full_adder full_adder_12 (
    .Cin(full_adder_13_cout), .a(A[4]), .b(xor_12_out), .Sum(result[4]), .Cout(full_adder_12_cout));
  xor xor_12 (xor_12_out, sub, B[4]);
  full_adder full_adder_13 (
    .Cin(full_adder_14_cout), .a(A[3]), .b(xor_13_out), .Sum(result[3]), .Cout(full_adder_13_cout));
  xor xor_13 (xor_13_out, sub, B[3]);
  full_adder full_adder_14 (
    .Cin(full_adder_15_cout), .a(A[2]), .b(xor_14_out), .Sum(result[2]), .Cout(full_adder_14_cout));
  xor xor_14 (xor_14_out, sub, B[2]);
  full_adder full_adder_15 (
    .Cin(full_adder_16_cout), .a(A[1]), .b(xor_15_out), .Sum(result[1]), .Cout(full_adder_15_cout));
  xor xor_15 (xor_15_out, sub, B[1]);
  full_adder full_adder_16 (.Cin(sub), .a(A[0]), .b(xor_16_out), .Sum(result[0]), .Cout(full_adder_16_cout));
  xor xor_16 (xor_16_out, sub, B[0]);

  // Other names for the same wires on the sheet: s0 = result[0]; s1 = result[1]; s2 = result[2]; s3 = result[3];
  //   s4 = result[4]; s5 = result[5]; s6 = result[6]; s7 = result[7]; s8 = result[8]; s9 = result[9];
  //   s10 = result[10]; s11 = result[11]; s12 = result[12]; s13 = result[13]; s14 = result[14]; s15 = result[15]
endmodule

module full_adder (
  input  Cin,
  input  a,
  input  b,
  output Sum,
  output Cout
);

  wire and_1_out, and_2_out, xor_1_out;

  and and_1 (and_1_out, b, a);
  xor xor_1 (xor_1_out, a, b);
  or or_1 (Cout, and_1_out, and_2_out);
  and and_2 (and_2_out, xor_1_out, Cin);
  xor xor_2 (Sum, Cin, xor_1_out);
endmodule

module shifter_circuit (
  input  [15:0] A,
  input  [2:0] shift_bit,
  output [15:0] result
);

  wire multiplexer_1_out, multiplexer_2_out, multiplexer_3_out, multiplexer_4_out, multiplexer_5_out,
       multiplexer_6_out, multiplexer_7_out, multiplexer_8_out, multiplexer_9_out, multiplexer_10_out,
       multiplexer_11_out, multiplexer_12_out, multiplexer_13_out, multiplexer_14_out, multiplexer_15_out,
       multiplexer_16_out, multiplexer_17_out, multiplexer_18_out, multiplexer_19_out, multiplexer_20_out,
       multiplexer_21_out, multiplexer_22_out, multiplexer_23_out, multiplexer_24_out, multiplexer_25_out,
       multiplexer_26_out, multiplexer_27_out, multiplexer_28_out, multiplexer_29_out, multiplexer_30_out,
       multiplexer_31_out, multiplexer_32_out;

  Multiplexer #(.enable("false")) multiplexer_1 (.in0(A[15]), .in1(A[11]), .out(multiplexer_1_out), .sel(shift_bit[2]));
  Multiplexer #(.enable("false")) multiplexer_2 (.in0(A[14]), .in1(A[10]), .out(multiplexer_2_out), .sel(shift_bit[2]));
  Multiplexer #(.enable("false")) multiplexer_3 (.in0(A[13]), .in1(A[9]), .out(multiplexer_3_out), .sel(shift_bit[2]));
  Multiplexer #(.enable("false")) multiplexer_4 (.in0(A[12]), .in1(A[8]), .out(multiplexer_4_out), .sel(shift_bit[2]));
  Multiplexer #(.enable("false")) multiplexer_5 (.in0(A[11]), .in1(A[7]), .out(multiplexer_5_out), .sel(shift_bit[2]));
  Multiplexer #(.enable("false")) multiplexer_6 (.in0(A[10]), .in1(A[6]), .out(multiplexer_6_out), .sel(shift_bit[2]));
  Multiplexer #(.enable("false")) multiplexer_7 (.in0(A[9]), .in1(A[5]), .out(multiplexer_7_out), .sel(shift_bit[2]));
  Multiplexer #(.enable("false")) multiplexer_8 (.in0(A[8]), .in1(A[4]), .out(multiplexer_8_out), .sel(shift_bit[2]));
  Multiplexer #(.enable("false")) multiplexer_9 (.in0(A[7]), .in1(A[3]), .out(multiplexer_9_out), .sel(shift_bit[2]));
  Multiplexer #(.enable("false")) multiplexer_10 (.in0(A[6]), .in1(A[2]), .out(multiplexer_10_out), .sel(shift_bit[2]));
  Multiplexer #(.enable("false")) multiplexer_11 (.in0(A[5]), .in1(A[1]), .out(multiplexer_11_out), .sel(shift_bit[2]));
  Multiplexer #(.enable("false")) multiplexer_12 (.in0(A[4]), .in1(A[0]), .out(multiplexer_12_out), .sel(shift_bit[2]));
  Multiplexer #(.enable("false")) multiplexer_13 (.in0(A[3]), .in1(1'b0), .out(multiplexer_13_out), .sel(shift_bit[2]));
  Multiplexer #(.enable("false")) multiplexer_14 (.in0(A[2]), .in1(1'b0), .out(multiplexer_14_out), .sel(shift_bit[2]));
  Multiplexer #(.enable("false")) multiplexer_15 (.in0(A[1]), .in1(1'b0), .out(multiplexer_15_out), .sel(shift_bit[2]));
  Multiplexer #(.enable("false")) multiplexer_16 (.in0(A[0]), .in1(1'b0), .out(multiplexer_16_out), .sel(shift_bit[2]));
  Multiplexer #(.enable("false")) multiplexer_17 (
    .in0(multiplexer_1_out), .in1(multiplexer_3_out), .out(multiplexer_17_out), .sel(shift_bit[1]));
  Multiplexer #(.enable("false")) multiplexer_18 (
    .in0(multiplexer_2_out), .in1(multiplexer_4_out), .out(multiplexer_18_out), .sel(shift_bit[1]));
  Multiplexer #(.enable("false")) multiplexer_19 (
    .in0(multiplexer_3_out), .in1(multiplexer_5_out), .out(multiplexer_19_out), .sel(shift_bit[1]));
  Multiplexer #(.enable("false")) multiplexer_20 (
    .in0(multiplexer_4_out), .in1(multiplexer_6_out), .out(multiplexer_20_out), .sel(shift_bit[1]));
  Multiplexer #(.enable("false")) multiplexer_21 (
    .in0(multiplexer_5_out), .in1(multiplexer_7_out), .out(multiplexer_21_out), .sel(shift_bit[1]));
  Multiplexer #(.enable("false")) multiplexer_22 (
    .in0(multiplexer_6_out), .in1(multiplexer_8_out), .out(multiplexer_22_out), .sel(shift_bit[1]));
  Multiplexer #(.enable("false")) multiplexer_23 (
    .in0(multiplexer_7_out), .in1(multiplexer_9_out), .out(multiplexer_23_out), .sel(shift_bit[1]));
  Multiplexer #(.enable("false")) multiplexer_24 (
    .in0(multiplexer_8_out), .in1(multiplexer_10_out), .out(multiplexer_24_out), .sel(shift_bit[1]));
  Multiplexer #(.enable("false")) multiplexer_25 (
    .in0(multiplexer_9_out), .in1(multiplexer_11_out), .out(multiplexer_25_out), .sel(shift_bit[1]));
  Multiplexer #(.enable("false")) multiplexer_26 (
    .in0(multiplexer_10_out), .in1(multiplexer_12_out), .out(multiplexer_26_out), .sel(shift_bit[1]));
  Multiplexer #(.enable("false")) multiplexer_27 (
    .in0(multiplexer_11_out), .in1(multiplexer_13_out), .out(multiplexer_27_out), .sel(shift_bit[1]));
  Multiplexer #(.enable("false")) multiplexer_28 (
    .in0(multiplexer_12_out), .in1(multiplexer_14_out), .out(multiplexer_28_out), .sel(shift_bit[1]));
  Multiplexer #(.enable("false")) multiplexer_29 (
    .in0(multiplexer_13_out), .in1(multiplexer_15_out), .out(multiplexer_29_out), .sel(shift_bit[1]));
  Multiplexer #(.enable("false")) multiplexer_30 (
    .in0(multiplexer_14_out), .in1(multiplexer_16_out), .out(multiplexer_30_out), .sel(shift_bit[1]));
  Multiplexer #(.enable("false")) multiplexer_31 (
    .in0(multiplexer_15_out), .in1(1'b0), .out(multiplexer_31_out), .sel(shift_bit[1]));
  Multiplexer #(.enable("false")) multiplexer_32 (
    .in0(multiplexer_16_out), .in1(1'b0), .out(multiplexer_32_out), .sel(shift_bit[1]));
  Multiplexer #(.enable("false")) multiplexer_33 (
    .in0(multiplexer_17_out), .in1(multiplexer_18_out), .out(result[15]), .sel(shift_bit[0]));
  Multiplexer #(.enable("false")) multiplexer_34 (
    .in0(multiplexer_18_out), .in1(multiplexer_19_out), .out(result[14]), .sel(shift_bit[0]));
  Multiplexer #(.enable("false")) multiplexer_35 (
    .in0(multiplexer_19_out), .in1(multiplexer_20_out), .out(result[13]), .sel(shift_bit[0]));
  Multiplexer #(.enable("false")) multiplexer_36 (
    .in0(multiplexer_20_out), .in1(multiplexer_21_out), .out(result[12]), .sel(shift_bit[0]));
  Multiplexer #(.enable("false")) multiplexer_37 (
    .in0(multiplexer_21_out), .in1(multiplexer_22_out), .out(result[11]), .sel(shift_bit[0]));
  Multiplexer #(.enable("false")) multiplexer_38 (
    .in0(multiplexer_22_out), .in1(multiplexer_23_out), .out(result[10]), .sel(shift_bit[0]));
  Multiplexer #(.enable("false")) multiplexer_39 (
    .in0(multiplexer_23_out), .in1(multiplexer_24_out), .out(result[9]), .sel(shift_bit[0]));
  Multiplexer #(.enable("false")) multiplexer_40 (
    .in0(multiplexer_24_out), .in1(multiplexer_25_out), .out(result[8]), .sel(shift_bit[0]));
  Multiplexer #(.enable("false")) multiplexer_41 (
    .in0(multiplexer_25_out), .in1(multiplexer_26_out), .out(result[7]), .sel(shift_bit[0]));
  Multiplexer #(.enable("false")) multiplexer_42 (
    .in0(multiplexer_26_out), .in1(multiplexer_27_out), .out(result[6]), .sel(shift_bit[0]));
  Multiplexer #(.enable("false")) multiplexer_43 (
    .in0(multiplexer_27_out), .in1(multiplexer_28_out), .out(result[5]), .sel(shift_bit[0]));
  Multiplexer #(.enable("false")) multiplexer_44 (
    .in0(multiplexer_28_out), .in1(multiplexer_29_out), .out(result[4]), .sel(shift_bit[0]));
  Multiplexer #(.enable("false")) multiplexer_45 (
    .in0(multiplexer_29_out), .in1(multiplexer_30_out), .out(result[3]), .sel(shift_bit[0]));
  Multiplexer #(.enable("false")) multiplexer_46 (
    .in0(multiplexer_30_out), .in1(multiplexer_31_out), .out(result[2]), .sel(shift_bit[0]));
  Multiplexer #(.enable("false")) multiplexer_47 (
    .in0(multiplexer_31_out), .in1(multiplexer_32_out), .out(result[1]), .sel(shift_bit[0]));
  Multiplexer #(.enable("false")) multiplexer_48 (
    .in0(multiplexer_32_out), .in1(1'b0), .out(result[0]), .sel(shift_bit[0]));

  // Other names for the same wires on the sheet: b0 = A[0]; b1 = A[1]; b2 = A[2]; b3 = A[3]; b4 = A[4]; b5 = A[5];
  //   b6 = A[6]; b7 = A[7]; b8 = A[8]; b9 = A[9]; b10 = A[10]; b11 = A[11]; b12 = A[12]; b13 = A[13]; b14 = A[14];
  //   b15 = A[15]; out_0 = result[0]; out_1 = result[1]; out_2 = result[2]; out_3 = result[3]; out_4 = result[4];
  //   out_5 = result[5]; out_6 = result[6]; out_7 = result[7]; out_8 = result[8]; out_9 = result[9];
  //   out_10 = result[10]; out_11 = result[11]; out_12 = result[12]; out_13 = result[13]; out_14 = result[14];
  //   out_15 = result[15]; s0 = shift_bit[0]; s1 = shift_bit[1]; s2 = shift_bit[2]
endmodule

module instruction_decoder (
  input  [15:0] instruction_code,
  output [2:0] Rt,
  output [15:0] address,
  output [2:0] Rs,
  output [3:0] opcode,
  output [2:0] Rd,
  output [5:0] Imm,
  output [2:0] shamt
);


  assign address = {4'b0000, instruction_code[11:0]};
  assign Imm = instruction_code[5:0];
  assign opcode = instruction_code[15:12];
  assign Rd = instruction_code[5:3];
  assign Rs = instruction_code[11:9];
  assign Rt = instruction_code[8:6];
  assign shamt = instruction_code[2:0];
endmodule

module signExtension (
  input  [5:0] input_val,
  output [15:0] result
);


  assign result = {{11{input_val[5]}}, input_val[4:0]};

  // Other names for the same wires on the sheet: sign = input_val[5]
endmodule
