// Logisim project my_adder.circ as structural Verilog: 2 circuits, main circuit main
module main (
  input  [15:0] B,
  input  [15:0] A,
  input  sub,
  output [15:0] result,
  output ovf
);

  wire C14, C15, full_adder_3_cout, full_adder_4_cout, full_adder_5_cout, full_adder_6_cout,
       full_adder_7_cout, full_adder_8_cout, full_adder_9_cout, full_adder_10_cout, full_adder_11_cout,
       full_adder_12_cout, full_adder_13_cout, full_adder_14_cout, full_adder_15_cout, full_adder_16_cout,
       xor_1_out, xor_3_out, xor_4_out, xor_5_out, xor_6_out, xor_7_out, xor_8_out, xor_9_out, xor_10_out,
       xor_11_out, xor_12_out, xor_13_out, xor_14_out, xor_15_out, xor_16_out, xor_17_out;

  full_adder full_adder_1 (.Cin(C14), .a(A[15]), .b(xor_1_out), .Sum(result[15]), .Cout(C15));
  xor xor_1 (xor_1_out, sub, B[15]);
  xor xor_2 (ovf, C14, C15);
  full_adder full_adder_2 (.Cin(full_adder_3_cout), .a(A[14]), .b(xor_3_out), .Sum(result[14]), .Cout(C14));
  xor xor_3 (xor_3_out, sub, B[14]);
  full_adder full_adder_3 (
    .Cin(full_adder_4_cout), .a(A[13]), .b(xor_4_out), .Sum(result[13]), .Cout(full_adder_3_cout));
  xor xor_4 (xor_4_out, sub, B[13]);
  full_adder full_adder_4 (
    .Cin(full_adder_5_cout), .a(A[12]), .b(xor_5_out), .Sum(result[12]), .Cout(full_adder_4_cout));
  xor xor_5 (xor_5_out, sub, B[12]);
  full_adder full_adder_5 (
    .Cin(full_adder_6_cout), .a(A[11]), .b(xor_6_out), .Sum(result[11]), .Cout(full_adder_5_cout));
  xor xor_6 (xor_6_out, sub, B[11]);
  full_adder full_adder_6 (
    .Cin(full_adder_7_cout), .a(A[10]), .b(xor_7_out), .Sum(result[10]), .Cout(full_adder_6_cout));
  xor xor_7 (xor_7_out, sub, B[10]);
  full_adder full_adder_7 (.Cin(full_adder_8_cout), .a(A[9]), .b(xor_8_out), .Sum(result[9]), .Cout(full_adder_7_cout));
  xor xor_8 (xor_8_out, sub, B[9]);
  full_adder full_adder_8 (.Cin(full_adder_9_cout), .a(A[8]), .b(xor_9_out), .Sum(result[8]), .Cout(full_adder_8_cout));
  xor xor_9 (xor_9_out, sub, B[8]);
  full_adder full_adder_9 (
    .Cin(full_adder_10_cout), .a(A[7]), .b(xor_10_out), .Sum(result[7]), .Cout(full_adder_9_cout));
  xor xor_10 (xor_10_out, sub, B[7]);
  full_adder full_adder_10 (
    .Cin(full_adder_11_cout), .a(A[6]), .b(xor_11_out), .Sum(result[6]), .Cout(full_adder_10_cout));
  xor xor_11 (xor_11_out, sub, B[6]);
  full_adder full_adder_11 (
    .Cin(full_adder_12_cout), .a(A[5]), .b(xor_12_out), .Sum(result[5]), .Cout(full_adder_11_cout));
  xor xor_12 (xor_12_out, sub, B[5]);
  full_adder full_adder_12 (
    .Cin(full_adder_13_cout), .a(A[4]), .b(xor_13_out), .Sum(result[4]), .Cout(full_adder_12_cout));
  xor xor_13 (xor_13_out, sub, B[4]);
  full_adder full_adder_13 (
    .Cin(full_adder_14_cout), .a(A[3]), .b(xor_14_out), .Sum(result[3]), .Cout(full_adder_13_cout));
  xor xor_14 (xor_14_out, sub, B[3]);
  full_adder full_adder_14 (
    .Cin(full_adder_15_cout), .a(A[2]), .b(xor_15_out), .Sum(result[2]), .Cout(full_adder_14_cout));
  xor xor_15 (xor_15_out, sub, B[2]);
  full_adder full_adder_15 (
    .Cin(full_adder_16_cout), .a(A[1]), .b(xor_16_out), .Sum(result[1]), .Cout(full_adder_15_cout));
  xor xor_16 (xor_16_out, sub, B[1]);
  full_adder full_adder_16 (.Cin(sub), .a(A[0]), .b(xor_17_out), .Sum(result[0]), .Cout(full_adder_16_cout));
  xor xor_17 (xor_17_out, sub, B[0]);

  // Other names for the same wires on the sheet: s0 = result[0]; s1 = result[1]; s2 = result[2]; s3 = result[3];
  //   s4 = result[4]; s5 = result[5]; s6 = result[6]; s7 = result[7]; s8 = result[8]; s9 = result[9];
  //   s10 = result[10]; s11 = result[11]; s12 = result[12]; s13 = result[13]; s14 = result[14]; s15 = result[15]
endmodule

module full_adder (
  input  Cin,
  input  a,
  input  b,
  output Sum,
  output Cout
);

  wire and_1_out, and_2_out, xor_1_out;

  and and_1 (and_1_out, b, a);
  xor xor_1 (xor_1_out, a, b);
  or or_1 (Cout, and_1_out, and_2_out);
  and and_2 (and_2_out, xor_1_out, Cin);
  xor xor_2 (Sum, Cin, xor_1_out);
endmodule
